// Digital circuit ALU.dig as structural Verilog
module ALU (
  input  A,
  input  B,
  input  A_2,
  input  B_2,
  input  A_3,
  input  B_3,
  input  A_4,
  input  B_4,
  input  A_5,
  input  B_5,
  input  A_6,
  input  B_6,
  input  A_7,
  input  B_7,
  input  A_8,
  input  B_8,
  input  Cin,
  input  A_9,
  input  B_9,
  input  A_10,
  input  B_10,
  input  A_11,
  input  B_11,
  input  A_12,
  input  B_12,
  input  A_13,
  input  B_13,
  input  A_14,
  input  B_14,
  input  A_15,
  input  B_15,
  input  A_16,
  input  B_16,
  input  Bin,
  input  A12,
  input  A13,
  input  A14,
  input  A15,
  input  A8,
  input  A9,
  input  A10,
  input  A11,
  input  B12,
  input  B13,
  input  B14,
  input  B15,
  input  B8,
  input  B9,
  input  B10,
  input  B11,
  input  Cin_2,
  input  [2:0] in_79,
  input  [7:0] in_80,
  input  [7:0] in_81,
  output Cout,
  output Sum,
  output Sum_2,
  output Sum_3,
  output Sum_4,
  output Sum_5,
  output Sum_6,
  output Sum_7,
  output Sum_8,
  output diff,
  output Bout,
  output diff_2,
  output diff_3,
  output diff_4,
  output diff_5,
  output diff_6,
  output diff_7,
  output diff_8,
  output Cout_2,
  output R15,
  output R14,
  output R13,
  output R12,
  output R11,
  output R10,
  output R9,
  output R8
);

  wire and_1_out, and_2_out, and_3_out, and_4_out, and_5_out, and_6_out, and_7_out, and_8_out, and_9_out,
       and_10_out, and_11_out, and_12_out, and_13_out, and_14_out, and_15_out, and_16_out, and_17_out,
       and_18_out, and_19_out, and_20_out, and_21_out, and_22_out, and_23_out, and_24_out, and_25_out,
       and_26_out, and_27_out, and_28_out, and_29_out, and_30_out, and_31_out, and_32_out, and_33_out,
       and_34_out, and_35_out, and_36_out, and_37_out, and_38_out, and_39_out, and_40_out, and_41_out,
       and_42_out, and_43_out, and_44_out, and_45_out, and_46_out, and_47_out, and_48_out, and_49_out,
       and_50_out, and_51_out, and_52_out, and_53_out, and_54_out, and_55_out, and_56_out, and_57_out,
       and_58_out, and_59_out, and_60_out, and_61_out, and_62_out, and_63_out, and_64_out, and_65_out,
       and_66_out, and_67_out, and_68_out, and_69_out, and_70_out, and_71_out, and_72_out, Div, Mult_t,
       Nand_t, not_1_out, not_2_out, not_3_out, not_4_out, not_5_out, not_6_out, not_7_out, not_8_out,
       not_9_out, not_10_out, not_11_out, not_12_out, not_13_out, not_14_out, not_15_out, not_16_out, SD, SE,
       Soma, Sub, xor_1_out, xor_2_out, xor_3_out, xor_4_out, xor_5_out, xor_6_out, xor_7_out, xor_8_out,
       xor_9_out, xor_11_out, xor_14_out, xor_16_out, xor_18_out, xor_20_out, xor_21_out, xor_22_out,
       xor_24_out, xor_25_out, xor_26_out, xor_27_out, xor_28_out, xor_31_out, xor_32_out, xor_33_out,
       xor_34_out, xor_35_out, xor_36_out, xor_37_out, xor_38_out, xor_39_out, xor_41_out, xor_43_out,
       xor_44_out, xor_45_out, xor_46_out, xor_47_out, xor_48_out, xor_49_out, xor_50_out, xor_51_out,
       xor_52_out, xor_54_out, xor_57_out, xor_62_out, xor_63_out, xor_64_out, xor_67_out, xor_68_out,
       xor_71_out, xor_73_out, xor_74_out, xor_75_out, xor_76_out, xor_78_out, xor_79_out, xor_80_out,
       xor_82_out, xor_83_out, xor_85_out, xor_86_out, xor_87_out, xor_89_out, xor_90_out, xor_91_out,
       xor_93_out, xor_94_out, xor_95_out, xor_97_out, xor_98_out, Xor_t;
  wire [7:0] MULT, NAND, R, Shift_D, Shift_E, Subt, Sum_t, XOR;

  and and_1 (and_1_out, A15, B15);
  and and_2 (and_2_out, B15, xor_24_out);
  and and_3 (and_3_out, A15, xor_24_out);
  xor xor_1 (xor_1_out, A14, B14);
  and and_4 (and_4_out, A14, B14);
  and and_5 (and_5_out, B14, xor_25_out);
  and and_6 (and_6_out, A14, xor_25_out);
  and and_7 (and_7_out, A13, B13);
  and and_8 (and_8_out, B13, xor_26_out);
  and and_9 (and_9_out, A13, xor_26_out);
  and and_10 (and_10_out, A12, B12);
  and and_11 (and_11_out, B12, xor_27_out);
  and and_12 (and_12_out, A12, xor_27_out);
  and and_13 (and_13_out, A11, B11);
  and and_14 (and_14_out, B11, xor_28_out);
  and and_15 (and_15_out, A11, xor_28_out);
  and and_16 (and_16_out, A10, B10);
  and and_17 (and_17_out, B10, xor_31_out);
  and and_18 (and_18_out, A10, xor_31_out);
  xor xor_2 (xor_2_out, A15, B15);
  xor xor_3 (xor_3_out, and_4_out, and_5_out);
  xor xor_4 (xor_4_out, A13, B13);
  xor xor_5 (xor_5_out, A12, B12);
  xor xor_6 (xor_6_out, A11, B11);
  xor xor_7 (xor_7_out, A10, B10);
  xor xor_8 (xor_8_out, A9, B9);
  and and_19 (and_19_out, A9, B9);
  and and_20 (and_20_out, B9, xor_32_out);
  and and_21 (and_21_out, A9, xor_32_out);
  xor xor_9 (xor_9_out, A8, B8);
  and and_22 (and_22_out, A8, B8);
  and and_23 (and_23_out, B8, Cin_2);
  and and_24 (and_24_out, A8, Cin_2);
  xor xor_10 (R15, xor_2_out, xor_24_out);
  xor xor_11 (xor_11_out, and_1_out, and_2_out);
  xor xor_12 (R14, xor_1_out, xor_25_out);
  xor xor_13 (R13, xor_4_out, xor_26_out);
  xor xor_14 (xor_14_out, and_7_out, and_8_out);
  xor xor_15 (R12, xor_5_out, xor_27_out);
  xor xor_16 (xor_16_out, and_10_out, and_11_out);
  xor xor_17 (R11, xor_6_out, xor_28_out);
  xor xor_18 (xor_18_out, and_13_out, and_14_out);
  xor xor_19 (R10, xor_7_out, xor_31_out);
  xor xor_20 (xor_20_out, and_16_out, and_17_out);
  xor xor_21 (xor_21_out, and_19_out, and_20_out);
  xor xor_22 (xor_22_out, and_22_out, and_23_out);
  xor xor_23 (Cout_2, xor_11_out, and_3_out);
  xor xor_24 (xor_24_out, xor_3_out, and_6_out);
  xor xor_25 (xor_25_out, xor_14_out, and_9_out);
  xor xor_26 (xor_26_out, xor_16_out, and_12_out);
  xor xor_27 (xor_27_out, xor_18_out, and_15_out);
  xor xor_28 (xor_28_out, xor_20_out, and_18_out);
  xor xor_29 (R9, xor_8_out, xor_32_out);
  xor xor_30 (R8, xor_9_out, Cin_2);
  xor xor_31 (xor_31_out, xor_21_out, and_21_out);
  xor xor_32 (xor_32_out, xor_22_out, and_24_out);
  not not_1 (not_1_out, A_10);
  not not_2 (not_2_out, A_10);
  not not_3 (not_3_out, A_11);
  not not_4 (not_4_out, A_11);
  not not_5 (not_5_out, A_9);
  not not_6 (not_6_out, A_9);
  and and_25 (and_25_out, B_10, xor_52_out);
  and and_26 (and_26_out, not_1_out, xor_52_out);
  and and_27 (and_27_out, not_2_out, B_10);
  and and_28 (and_28_out, B_11, xor_54_out);
  and and_29 (and_29_out, not_3_out, xor_54_out);
  and and_30 (and_30_out, not_4_out, B_11);
  and and_31 (and_31_out, B_12, xor_62_out);
  and and_32 (and_32_out, not_7_out, xor_62_out);
  not not_7 (not_7_out, A_12);
  and and_33 (and_33_out, not_8_out, B_12);
  not not_8 (not_8_out, A_12);
  and and_34 (and_34_out, B_13, xor_57_out);
  and and_35 (and_35_out, not_9_out, xor_57_out);
  not not_9 (not_9_out, A_13);
  and and_36 (and_36_out, not_10_out, B_13);
  not not_10 (not_10_out, A_13);
  and and_37 (and_37_out, B_14, xor_63_out);
  and and_38 (and_38_out, not_11_out, xor_63_out);
  not not_11 (not_11_out, A_14);
  and and_39 (and_39_out, not_12_out, B_14);
  not not_12 (not_12_out, A_14);
  and and_40 (and_40_out, B_15, xor_64_out);
  and and_41 (and_41_out, not_13_out, xor_64_out);
  not not_13 (not_13_out, A_15);
  and and_42 (and_42_out, not_14_out, B_15);
  not not_14 (not_14_out, A_15);
  and and_43 (and_43_out, B_16, Bin);
  and and_44 (and_44_out, not_15_out, Bin);
  not not_15 (not_15_out, A_16);
  and and_45 (and_45_out, not_16_out, B_16);
  not not_16 (not_16_out, A_16);
  and and_46 (and_46_out, B_9, xor_51_out);
  and and_47 (and_47_out, not_5_out, xor_51_out);
  and and_48 (and_48_out, not_6_out, B_9);
  xor xor_33 (xor_33_out, A_10, B_10);
  xor xor_34 (xor_34_out, A_11, B_11);
  xor xor_35 (xor_35_out, A_12, B_12);
  xor xor_36 (xor_36_out, A_13, B_13);
  xor xor_37 (xor_37_out, A_14, B_14);
  xor xor_38 (xor_38_out, A_15, B_15);
  xor xor_39 (xor_39_out, A_16, B_16);
  xor xor_40 (diff_2, xor_33_out, xor_52_out);
  xor xor_41 (xor_41_out, and_25_out, and_26_out);
  xor xor_42 (diff_3, xor_34_out, xor_54_out);
  xor xor_43 (xor_43_out, and_28_out, and_29_out);
  xor xor_44 (xor_44_out, and_31_out, and_32_out);
  xor xor_45 (xor_45_out, and_34_out, and_35_out);
  xor xor_46 (xor_46_out, and_37_out, and_38_out);
  xor xor_47 (xor_47_out, and_40_out, and_41_out);
  xor xor_48 (xor_48_out, and_43_out, and_44_out);
  xor xor_49 (xor_49_out, A_9, B_9);
  xor xor_50 (xor_50_out, and_46_out, and_47_out);
  xor xor_51 (xor_51_out, xor_41_out, and_27_out);
  xor xor_52 (xor_52_out, xor_43_out, and_30_out);
  xor xor_53 (diff_4, xor_35_out, xor_62_out);
  xor xor_54 (xor_54_out, xor_44_out, and_33_out);
  xor xor_55 (diff_5, xor_36_out, xor_57_out);
  xor xor_56 (diff_6, xor_37_out, xor_63_out);
  xor xor_57 (xor_57_out, xor_46_out, and_39_out);
  xor xor_58 (diff_7, xor_38_out, xor_64_out);
  xor xor_59 (diff_8, xor_39_out, Bin);
  xor xor_60 (diff, xor_49_out, xor_51_out);
  xor xor_61 (Bout, xor_50_out, and_48_out);
  xor xor_62 (xor_62_out, xor_45_out, and_36_out);
  xor xor_63 (xor_63_out, xor_47_out, and_42_out);
  xor xor_64 (xor_64_out, xor_48_out, and_45_out);
  Seven_Seg_Hex seven_seg_hex_1 (.d(in_80[7:4]), .dp(1'b0));
  LED led_1 (.in(in_80[7]));
  // Somador_8bits somador_8bits_1: pin names not known; wires that end beside it: in_80, in_81, Soma, 1'b0, Sum_t
  Seven_Seg_Hex seven_seg_hex_2 (.d(in_80[3:0]), .dp(1'b0));
  LED led_2 (.in(in_80[6]));
  LED led_3 (.in(in_80[5]));
  LED led_4 (.in(in_80[4]));
  LED led_5 (.in(in_80[3]));
  LED led_6 (.in(in_80[2]));
  LED led_7 (.in(in_80[1]));
  // Subtrator_8bits subtrator_8bits_1: pin names not known; wires that end beside it: 1'b0, in_80, in_81, Sub, Subt
  Seven_Seg_Hex seven_seg_hex_3 (.d(in_81[7:4]), .dp(1'b0));
  LED led_8 (.in(in_80[0]));
  Seven_Seg_Hex seven_seg_hex_4 (.d(in_81[3:0]), .dp(1'b0));
  LED led_9 (.in(in_81[7]));
  LED led_10 (.in(in_81[6]));
  // Shift_Direita shift_direita_1: pin names not known; wires that end beside it: SD, in_80, Shift_D
  LED led_11 (.in(in_81[5]));
  LED led_12 (.in(in_81[4]));
  Seven_Seg_Hex seven_seg_hex_5 (.d(R[7:4]), .dp(1'b0));
  LED led_13 (.in(in_81[3]));
  LED led_14 (.in(in_81[2]));
  Seven_Seg_Hex seven_seg_hex_6 (.d(R[3:0]), .dp(1'b0));
  LED led_15 (.in(in_81[1]));
  LED led_16 (.in(in_81[0]));
  // Shift_Esquerda shift_esquerda_1: pin names not known; wires that end beside it: in_81, SE, Shift_E
  LED led_17 (.in(R[7]));
  LED led_18 (.in(R[6]));
  LED led_19 (.in(R[5]));
  LED led_20 (.in(R[4]));
  // XOR xor_65: pin names not known; wires that end beside it: in_80, in_81, Xor_t, XOR
  // seletor seletor_1: pin names not known; wires that end beside it: in_79, Soma, Sub, Mult_t, Div, SD, SE, Nand_t, Xor_t
  LED led_21 (.in(R[3]));
  LED led_22 (.in(R[2]));
  LED led_23 (.in(R[1]));
  LED led_24 (.in(R[0]));
  // NAND nand_1: pin names not known; wires that end beside it: in_80, in_81, Nand_t, NAND
  assign R = Sum_t ^ Subt ^ Shift_D ^ Shift_E ^ XOR ^ NAND ^ MULT;  // XOr xor_66, 8 bits wide
  // Multiplicador_4bits multiplicador_4bits_1: pin names not known; wires that end beside it: in_81, in_80, Mult_t, MULT
  xor xor_67 (xor_67_out, A, B);
  and and_49 (and_49_out, A, B);
  and and_50 (and_50_out, B, xor_74_out);
  and and_51 (and_51_out, A, xor_74_out);
  xor xor_68 (xor_68_out, and_49_out, and_50_out);
  xor xor_69 (Sum, xor_67_out, xor_74_out);
  xor xor_70 (Cout, xor_68_out, and_51_out);
  and and_52 (and_52_out, A_2, B_2);
  and and_53 (and_53_out, B_2, xor_78_out);
  and and_54 (and_54_out, A_2, xor_78_out);
  xor xor_71 (xor_71_out, A_2, B_2);
  xor xor_72 (Sum_2, xor_71_out, xor_78_out);
  xor xor_73 (xor_73_out, and_52_out, and_53_out);
  xor xor_74 (xor_74_out, xor_73_out, and_54_out);
  xor xor_75 (xor_75_out, A_3, B_3);
  and and_55 (and_55_out, A_3, B_3);
  and and_56 (and_56_out, B_3, xor_82_out);
  and and_57 (and_57_out, A_3, xor_82_out);
  xor xor_76 (xor_76_out, and_55_out, and_56_out);
  xor xor_77 (Sum_3, xor_75_out, xor_82_out);
  xor xor_78 (xor_78_out, xor_76_out, and_57_out);
  xor xor_79 (xor_79_out, A_4, B_4);
  and and_58 (and_58_out, A_4, B_4);
  and and_59 (and_59_out, B_4, xor_86_out);
  and and_60 (and_60_out, A_4, xor_86_out);
  xor xor_80 (xor_80_out, and_58_out, and_59_out);
  xor xor_81 (Sum_4, xor_79_out, xor_86_out);
  xor xor_82 (xor_82_out, xor_80_out, and_60_out);
  and and_61 (and_61_out, A_5, B_5);
  and and_62 (and_62_out, B_5, xor_90_out);
  and and_63 (and_63_out, A_5, xor_90_out);
  xor xor_83 (xor_83_out, A_5, B_5);
  xor xor_84 (Sum_5, xor_83_out, xor_90_out);
  xor xor_85 (xor_85_out, and_61_out, and_62_out);
  xor xor_86 (xor_86_out, xor_85_out, and_63_out);
  and and_64 (and_64_out, A_6, B_6);
  and and_65 (and_65_out, B_6, xor_94_out);
  and and_66 (and_66_out, A_6, xor_94_out);
  xor xor_87 (xor_87_out, A_6, B_6);
  xor xor_88 (Sum_6, xor_87_out, xor_94_out);
  xor xor_89 (xor_89_out, and_64_out, and_65_out);
  xor xor_90 (xor_90_out, xor_89_out, and_66_out);
  and and_67 (and_67_out, A_7, B_7);
  and and_68 (and_68_out, B_7, xor_98_out);
  and and_69 (and_69_out, A_7, xor_98_out);
  xor xor_91 (xor_91_out, A_7, B_7);
  xor xor_92 (Sum_7, xor_91_out, xor_98_out);
  xor xor_93 (xor_93_out, and_67_out, and_68_out);
  xor xor_94 (xor_94_out, xor_93_out, and_69_out);
  and and_70 (and_70_out, A_8, B_8);
  and and_71 (and_71_out, B_8, Cin);
  and and_72 (and_72_out, A_8, Cin);
  xor xor_95 (xor_95_out, A_8, B_8);
  xor xor_96 (Sum_8, xor_95_out, Cin);
  xor xor_97 (xor_97_out, and_70_out, and_71_out);
  xor xor_98 (xor_98_out, xor_97_out, and_72_out);

  // Other names for the same wires on the sheet: A_t[7:0] = in_80; B_t[7:0] = in_81

  // Notes on the sheet:
  //   Operacoes
  //   Hexa primeiro numero
  //   Binario primeiro numero
  //   Hexa segundo numero
  //   Binario segundo numero
  //   Hexa resultado
  //   Binario resultado
  //   Seletor
endmodule
